// Logisim project control.circ as structural Verilog: 4 circuits, main circuit main
module main (
  input  Start,
  input  Product0,
  input  EndLoop,
  input  Reset,
  input  Clk,
  output AddLeftAndPlace,
  output ShiftRight,
  output Counter_plus_plus,
  output Sm,
  output Enm,
  output Enp,
  output Sd,
  output Reset_2
);

  wire not_1_out, not_2_out, not_3_out, state0_out;
  wire [2:0] n0_1_out, register_1_q;

  N2 n2_1 (
    .s2(register_1_q[2]), .s1(register_1_q[1]), .s0(register_1_q[0]), .Out(n0_1_out[2]), .EndLoop(EndLoop),
    .Reset(Reset));
  N1 n1_1 (.s2(register_1_q[2]), .s1(register_1_q[1]), .s0(register_1_q[0]), .Out(n0_1_out[1]));
  N0 n0_1 (
    .s2(register_1_q[2]), .s1(register_1_q[1]), .s0(register_1_q[0]), .Start(Start), .EndLoop(EndLoop),
    .Out(n0_1_out[0]), .pd(Product0), .Reset(Reset));
  Register #(.width(3)) register_1 (.D(n0_1_out), .Q(register_1_q), .clk(Clk));  // open: en, clr
  not not_1 (not_1_out, register_1_q[0]);
  not not_2 (not_2_out, register_1_q[1]);
  not not_3 (not_3_out, register_1_q[2]);
  and state0 (state0_out, not_1_out, not_2_out, not_3_out);
  and state2 (AddLeftAndPlace, not_1_out, register_1_q[1], not_3_out);
  and state3 (Sd, register_1_q[0], register_1_q[1], not_3_out);
  and state4 (Counter_plus_plus, not_1_out, not_2_out, register_1_q[2]);
  or or_1 (Enm, state0_out, Sd);
  or or_2 (Enp, AddLeftAndPlace, Sd);

  assign Reset_2 = Reset;
  assign ShiftRight = Sd;
  assign Sm = Sd;
endmodule

module N2 (
  input  s2,
  input  s1,
  input  s0,
  input  EndLoop,
  input  Reset,
  output Out
);

  wire and_1_out, and_2_out, and_3_out, not_1_out, not_2_out, not_3_out, not_4_out;

  not not_1 (not_1_out, s2);
  not not_2 (not_2_out, s1);
  not not_3 (not_3_out, s0);
  not not_4 (not_4_out, Reset);
  and and_1 (and_1_out, not_1_out, s1, s0);
  and and_2 (and_2_out, s2, not_2_out, EndLoop, not_3_out);
  and and_3 (and_3_out, s2, not_2_out, not_4_out, s0);
  or or_1 (Out, and_1_out, and_3_out, and_2_out);
endmodule

module N1 (
  input  s2,
  input  s1,
  input  s0,
  output Out
);

  wire and_1_out, and_2_out, not_1_out, not_2_out, not_3_out;

  not not_1 (not_1_out, s2);
  not not_2 (not_2_out, s1);
  not not_3 (not_3_out, s0);
  and and_1 (and_1_out, not_1_out, not_2_out, s0);
  and and_2 (and_2_out, not_1_out, s1, not_3_out);
  or or_1 (Out, and_1_out, and_2_out);
endmodule

module N0 (
  input  s2,
  input  s1,
  input  s0,
  input  Start,
  input  EndLoop,
  input  pd,
  input  Reset,
  output Out
);

  wire and_1_out, and_2_out, and_3_out, and_4_out, and_5_out, and_6_out, not_1_out, not_2_out, not_3_out,
       not_4_out, not_5_out, not_6_out;

  not not_1 (not_1_out, s2);
  not not_2 (not_2_out, s1);
  not not_3 (not_3_out, s0);
  not not_4 (not_4_out, EndLoop);
  not not_5 (not_5_out, pd);
  not not_6 (not_6_out, Reset);
  and and_1 (and_1_out, not_1_out, not_2_out, not_3_out, Start);
  and and_2 (and_2_out, not_1_out, not_2_out, s0, not_5_out);
  and and_3 (and_3_out, not_1_out, s1, not_3_out);
  and and_4 (and_4_out, s2, not_2_out, not_3_out, not_4_out);
  and and_5 (and_5_out, s2, not_2_out, not_3_out, EndLoop);
  and and_6 (and_6_out, s2, not_2_out, not_6_out, s0);
  or or_1 (Out, and_5_out, and_1_out, and_2_out, and_3_out, and_4_out, and_6_out);
endmodule
