// Logisim project datapath.circ as structural Verilog: 5 circuits, main circuit main
module main (
  input  [31:0] Multiplicand,
  input  Sd,
  input  [31:0] Multiplier,
  input  ShiftRight,
  input  AddLeftAndPlace,
  input  Enp,
  input  Sm,
  input  Enm,
  input  Reset,
  input  Counter_plus_plus,
  input  Clk,
  output Product0,
  output [31:0] ProductHigh,
  output EndLoop,
  output [31:0] ProductLow
);

  wire [31:0] mathpath_1_outhigh, mathpath_1_outlow, multiplexer_1_out, multiplexer_2_out;

  Multiplexer #(.width(32)) multiplexer_1 (
    .in0(Multiplicand), .in1({ProductLow[31:1], Product0}), .out(multiplexer_1_out), .sel(Sd));  // open: en
  MathPath mathpath_1 (
    .ProductHigh(ProductHigh), .Multiplicand(multiplexer_1_out), .Add(AddLeftAndPlace),
    .ShiftRight(ShiftRight), .OutHigh(mathpath_1_outhigh), .OutLow(mathpath_1_outlow));
  Register #(.width(32)) u_ProductHigh (.D(mathpath_1_outhigh), .en(Enp), .Q(ProductHigh), .clk(Clk), .clr(Reset));
  Multiplexer #(.width(32)) multiplexer_2 (
    .in0(Multiplier), .in1(mathpath_1_outlow), .out(multiplexer_2_out), .sel(Sm));  // open: en
  Register #(.width(32)) u_Multiplier (
    .D(multiplexer_2_out), .en(Enm), .Q({ProductLow[31:1], Product0}), .clk(Clk));  // open: clr
  Counter #(.width(5), .max('h1f)) counter_1 (
    .count(Counter_plus_plus), .carry(EndLoop), .clk(Clk));  // open: load, D, Q, clr

  assign ProductLow[0] = Product0;
endmodule

module MathPath (
  input  [31:0] ProductHigh,
  input  [31:0] Multiplicand,
  input  ShiftRight,
  input  Add,
  output [31:0] OutHigh,
  output [31:0] OutLow
);

  wire [31:0] adder32_1_out, shifter64_1_outhigh;

  Shifter64 shifter64_1 (.InHigh(ProductHigh), .InLow(Multiplicand), .OutHigh(shifter64_1_outhigh), .OutLow(OutLow));
  Adder32 adder32_1 (.a(ProductHigh), .b(Multiplicand), .out(adder32_1_out));
  Multiplexer #(.select(2), .width(32)) multiplexer_1 (
    .in0(ProductHigh), .in1(shifter64_1_outhigh), .in2(adder32_1_out), .out(OutHigh), .sel({Add, ShiftRight}));  // open: in3, en
endmodule

module Shifter64 (
  input  [31:0] InHigh,
  input  [31:0] InLow,
  output [31:0] OutHigh,
  output [31:0] OutLow
);


  assign OutHigh = {1'b0, InHigh[31:1]};
  assign OutLow = {InHigh[0], InLow[31:1]};
endmodule

module Adder32 (
  input  [31:0] a,
  input  [31:0] b,
  output [31:0] out
);

  wire fulladder_2_cout, fulladder_3_cout, fulladder_4_cout, fulladder_5_cout, fulladder_6_cout,
       fulladder_7_cout, fulladder_8_cout, fulladder_9_cout, fulladder_10_cout, fulladder_11_cout,
       fulladder_12_cout, fulladder_13_cout, fulladder_14_cout, fulladder_15_cout, fulladder_16_cout,
       fulladder_17_cout, fulladder_18_cout, fulladder_19_cout, fulladder_20_cout, fulladder_21_cout,
       fulladder_22_cout, fulladder_23_cout, fulladder_24_cout, fulladder_25_cout, fulladder_26_cout,
       fulladder_27_cout, fulladder_28_cout, fulladder_29_cout, fulladder_30_cout, fulladder_31_cout,
       fulladder_32_cout;

  FullAdder fulladder_1 (.a(a[31]), .b(b[31]), .cin(fulladder_2_cout), .out(out[31]));  // open: cout
  FullAdder fulladder_2 (.a(a[30]), .b(b[30]), .cin(fulladder_3_cout), .out(out[30]), .cout(fulladder_2_cout));
  FullAdder fulladder_3 (.a(a[29]), .b(b[29]), .cin(fulladder_5_cout), .out(out[29]), .cout(fulladder_3_cout));
  FullAdder fulladder_4 (.a(a[27]), .b(b[27]), .cin(fulladder_6_cout), .out(out[27]), .cout(fulladder_4_cout));
  FullAdder fulladder_5 (.a(a[28]), .b(b[28]), .cin(fulladder_4_cout), .out(out[28]), .cout(fulladder_5_cout));
  FullAdder fulladder_6 (.a(a[26]), .b(b[26]), .cin(fulladder_7_cout), .out(out[26]), .cout(fulladder_6_cout));
  FullAdder fulladder_7 (.a(a[25]), .b(b[25]), .cin(fulladder_9_cout), .out(out[25]), .cout(fulladder_7_cout));
  FullAdder fulladder_8 (.a(a[23]), .b(b[23]), .cin(fulladder_10_cout), .out(out[23]), .cout(fulladder_8_cout));
  FullAdder fulladder_9 (.a(a[24]), .b(b[24]), .cin(fulladder_8_cout), .out(out[24]), .cout(fulladder_9_cout));
  FullAdder fulladder_10 (.a(a[22]), .b(b[22]), .cin(fulladder_11_cout), .out(out[22]), .cout(fulladder_10_cout));
  FullAdder fulladder_11 (.a(a[21]), .b(b[21]), .cin(fulladder_13_cout), .out(out[21]), .cout(fulladder_11_cout));
  FullAdder fulladder_12 (.a(a[19]), .b(b[19]), .cin(fulladder_14_cout), .out(out[19]), .cout(fulladder_12_cout));
  FullAdder fulladder_13 (.a(a[20]), .b(b[20]), .cin(fulladder_12_cout), .out(out[20]), .cout(fulladder_13_cout));
  FullAdder fulladder_14 (.a(a[18]), .b(b[18]), .cin(fulladder_15_cout), .out(out[18]), .cout(fulladder_14_cout));
  FullAdder fulladder_15 (.a(a[17]), .b(b[17]), .cin(fulladder_16_cout), .out(out[17]), .cout(fulladder_15_cout));
  FullAdder fulladder_16 (.a(a[16]), .b(b[16]), .cin(fulladder_17_cout), .out(out[16]), .cout(fulladder_16_cout));
  FullAdder fulladder_17 (.a(a[15]), .b(b[15]), .cin(fulladder_18_cout), .out(out[15]), .cout(fulladder_17_cout));
  FullAdder fulladder_18 (.a(a[14]), .b(b[14]), .cin(fulladder_19_cout), .out(out[14]), .cout(fulladder_18_cout));
  FullAdder fulladder_19 (.a(a[13]), .b(b[13]), .cin(fulladder_20_cout), .out(out[13]), .cout(fulladder_19_cout));
  FullAdder fulladder_20 (.a(a[12]), .b(b[12]), .cin(fulladder_21_cout), .out(out[12]), .cout(fulladder_20_cout));
  FullAdder fulladder_21 (.a(a[11]), .b(b[11]), .cin(fulladder_22_cout), .out(out[11]), .cout(fulladder_21_cout));
  FullAdder fulladder_22 (.a(a[10]), .b(b[10]), .cin(fulladder_23_cout), .out(out[10]), .cout(fulladder_22_cout));
  FullAdder fulladder_23 (.a(a[9]), .b(b[9]), .cin(fulladder_24_cout), .out(out[9]), .cout(fulladder_23_cout));
  FullAdder fulladder_24 (.a(a[8]), .b(b[8]), .cin(fulladder_25_cout), .out(out[8]), .cout(fulladder_24_cout));
  FullAdder fulladder_25 (.a(a[7]), .b(b[7]), .cin(fulladder_26_cout), .out(out[7]), .cout(fulladder_25_cout));
  FullAdder fulladder_26 (.a(a[6]), .b(b[6]), .cin(fulladder_27_cout), .out(out[6]), .cout(fulladder_26_cout));
  FullAdder fulladder_27 (.a(a[5]), .b(b[5]), .cin(fulladder_28_cout), .out(out[5]), .cout(fulladder_27_cout));
  FullAdder fulladder_28 (.a(a[4]), .b(b[4]), .cin(fulladder_29_cout), .out(out[4]), .cout(fulladder_28_cout));
  FullAdder fulladder_29 (.a(a[3]), .b(b[3]), .cin(fulladder_30_cout), .out(out[3]), .cout(fulladder_29_cout));
  FullAdder fulladder_30 (.a(a[2]), .b(b[2]), .cin(fulladder_31_cout), .out(out[2]), .cout(fulladder_30_cout));
  FullAdder fulladder_31 (.a(a[1]), .b(b[1]), .cin(fulladder_32_cout), .out(out[1]), .cout(fulladder_31_cout));
  FullAdder fulladder_32 (.a(a[0]), .b(b[0]), .cin(1'b0), .out(out[0]), .cout(fulladder_32_cout));
endmodule

module FullAdder (
  input  a,
  input  b,
  input  cin,
  output out,
  output cout
);

  wire and_1_out, and_2_out, and_3_out, and_4_out, and_5_out, and_6_out, and_7_out, not_1_out, not_2_out,
       not_3_out;

  not not_1 (not_1_out, a);
  not not_2 (not_2_out, b);
  not not_3 (not_3_out, cin);
  and and_1 (and_1_out, not_1_out, not_2_out, cin);
  and and_2 (and_2_out, not_1_out, b, not_3_out);
  and and_3 (and_3_out, a, not_2_out, not_3_out);
  and and_4 (and_4_out, a, b, cin);
  and and_5 (and_5_out, not_1_out, b, cin);
  and and_6 (and_6_out, a, not_2_out, cin);
  and and_7 (and_7_out, a, b);
  or or_1 (out, and_1_out, and_2_out, and_3_out, and_4_out);
  or or_2 (cout, and_5_out, and_6_out, and_7_out);
endmodule
