// Logisim project mult32.circ as structural Verilog: 1 circuit, main circuit main
module main (
  input  [31:0] Multiplier,
  input  [31:0] Multiplicand,
  output [31:0] ProductHigh,
  output [31:0] ProductLow
);

  wire clock_1_out, main_1_endloop, main_1_product0, main_2_addleftandplace, main_2_counter_plus_plus,
       main_2_enm, main_2_enp, main_2_reset_2, main_2_sd, main_2_shiftright, main_2_sm, Reset_out, Start_out;

  // Probe on Multiplier
  Clock clock_1 (.out(clock_1_out));
  datapath_main main_1 (
    .Product0(main_1_product0), .ProductHigh(ProductHigh), .ProductLow(ProductLow),
    .Counter_plus_plus(main_2_counter_plus_plus), .Clk(clock_1_out), .EndLoop(main_1_endloop),
    .AddLeftAndPlace(main_2_addleftandplace), .ShiftRight(main_2_shiftright), .Multiplicand(Multiplicand),
    .Multiplier(Multiplier), .Sm(main_2_sm), .Enm(main_2_enm), .Enp(main_2_enp), .Sd(main_2_sd),
    .Reset(main_2_reset_2));
  // Probe on ProductHigh
  // Probe on Multiplicand
  // Probe on ProductLow
  Button Start (.out(Start_out));
  control_main main_2 (
    .Product0(main_1_product0), .AddLeftAndPlace(main_2_addleftandplace), .ShiftRight(main_2_shiftright),
    .Start(Start_out), .Clk(clock_1_out), .Counter_plus_plus(main_2_counter_plus_plus),
    .EndLoop(main_1_endloop), .Sm(main_2_sm), .Enm(main_2_enm), .Enp(main_2_enp), .Sd(main_2_sd),
    .Reset(Reset_out), .Reset_2(main_2_reset_2));
  Button Reset (.out(Reset_out));

  // Notes on the sheet:
  //   OUTPUT
  //   Unsigned Number Multiplier
  //   Made by Rahmet Ali Olmez
  //   12/2020
endmodule
